// Logisim project Controller.circ as structural Verilog: 1 circuit, main circuit Controller
module Controller (
  input  [15:0] Inst,
  input  [3:0] FlagsIn,
  input  Clk,
  input  Reset,
  input  [31:0] R0,
  input  [31:0] R1,
  input  [31:0] R2,
  input  [31:0] R3,
  input  [31:0] R4,
  input  [31:0] R5,
  input  [31:0] R6,
  input  [31:0] R7,
  input  [31:0] RAM_Value,
  output Carry,
  output DP_Shift,
  output Imm32_Enable,
  output [4:0] Imm5,
  output [31:0] Imm32,
  output [3:0] ALU_Opcode,
  output [2:0] Rm,
  output [2:0] Rn,
  output [2:0] Rd,
  output [3:0] Flags,
  output [31:0] RAM_Addr,
  output Load,
  output Store,
  output PC_Hold,
  output [31:0] SP,
  output [31:0] PC
);

  wire and_1_out, and_2_out, and_3_out, and_4_out, and_6_out, comparator_1_eq, comparator_2_eq,
       comparator_3_eq, comparator_4_eq, conditional_1_verified, load_address_1_imm32_enable, not_1_out,
       not_2_out, opcode_decoder_1_conditional, opcode_decoder_1_data_processing,
       opcode_decoder_1_high_register_op, opcode_decoder_1_load_address, opcode_decoder_1_load_store,
       opcode_decoder_1_long_branch, opcode_decoder_1_shift, opcode_decoder_1_sp_address, or_2_out, or_4_out,
       or_5_out, shift_add_sub_mov_1_carry, shift_add_sub_mov_1_imm32_enable, sp_address_1_write_enable;
  wire [2:0] controlled_buffer_2_out, controlled_buffer_3_out, data_processing_1_rd, data_processing_1_rm,
       data_processing_1_rn, load_address_1_rd, load_store_1_rmd, shift_add_sub_mov_1_rd,
       shift_add_sub_mov_1_rm, shift_add_sub_mov_1_rn;
  wire [3:0] data_processing_1_alu_opcode, data_processing_1_flags_update_mask, load_address_1_alu_opcode,
       or_1_out, pull_resistor_4_node, pull_resistor_5_node, shift_add_sub_mov_1_alu_opcode,
       shift_add_sub_mov_1_flags_update_mask;
  wire [10:0] conditional_1_offset, or_3_out, pull_resistor_1_node;
  wire [31:0] adder_1_out, adder_2_out, adder_3_out, adder_4_out, adder_5_out, and_5_out, bit_extender_1_out,
       controlled_buffer_5_out, controlled_buffer_7_out, controlled_buffer_8_out, load_address_1_imm32,
       load_store_1_imm32, LR_Value, multiplexer_1_out, multiplexer_2_out, multiplexer_4_out,
       multiplier_1_out, negator_1_out, or_13_out, pull_resistor_7_node, shift_add_sub_mov_1_imm32,
       sp_address_1_new_stack_pointer;

  Register #(.width(32)) Stack_Pointer (
    .D(sp_address_1_new_stack_pointer), .en(sp_address_1_write_enable), .clk(Clk), .Q(SP), .clr(Reset));
  Opcode_Decoder opcode_decoder_1 (
    .Opcode(Inst[15:9]), .Shift(opcode_decoder_1_shift), .Data_Processing(opcode_decoder_1_data_processing),
    .Load_Store(opcode_decoder_1_load_store), .SP_Address(opcode_decoder_1_sp_address),
    .Conditional(opcode_decoder_1_conditional), .Load_Address(opcode_decoder_1_load_address),
    .Long_Branch(opcode_decoder_1_long_branch), .High_Register_Op(opcode_decoder_1_high_register_op));
  assign or_1_out = data_processing_1_flags_update_mask | shift_add_sub_mov_1_flags_update_mask;  // OR_Gate or_1, 4 bits wide
  Comparator #(.width(4)) comparator_1 (.a(Inst[9:6]), .b(4'b1101), .eq(comparator_1_eq));  // open: gt, lt
  Comparator #(.width(4)) comparator_2 (.a(Inst[9:6]), .b(4'b1000), .eq(comparator_2_eq));  // open: gt, lt
  Comparator #(.width(4)) comparator_3 (.a(Inst[9:6]), .b(4'b1001), .eq(comparator_3_eq));  // open: gt, lt
  Comparator #(.width(4)) comparator_4 (.a(Inst[9:6]), .b(4'b1010), .eq(comparator_4_eq));  // open: gt, lt
  Pull_Resistor pull_resistor_1 (.node(pull_resistor_1_node));
  assign pull_resistor_1_node = opcode_decoder_1_long_branch ? Inst[10:0] : 11'bz;  // Controlled_Buffer controlled_buffer_1
  and and_1 (and_1_out, comparator_1_eq, opcode_decoder_1_high_register_op);
  and and_2 (and_2_out, comparator_2_eq, opcode_decoder_1_high_register_op);
  or or_2 (or_2_out, and_2_out, and_3_out);
  assign controlled_buffer_2_out = or_2_out ? Inst[2:0] : 3'bz;  // Controlled_Buffer controlled_buffer_2
  assign controlled_buffer_3_out = and_2_out ? Inst[5:3] : 3'bz;  // Controlled_Buffer controlled_buffer_3
  and and_3 (and_3_out, comparator_3_eq, opcode_decoder_1_high_register_op);
  and and_4 (and_4_out, comparator_4_eq, opcode_decoder_1_high_register_op);
  Conditional conditional_1 (
    .Offset(conditional_1_offset), .Verified(conditional_1_verified), .Instruction(Inst), .Z(Flags[2]),
    .C(Flags[1]), .N(Flags[3]), .V(Flags[0]), .Enable(opcode_decoder_1_conditional));
  Pull_Resistor pull_resistor_2 (.node(controlled_buffer_2_out));
  Pull_Resistor pull_resistor_3 (.node(controlled_buffer_3_out));
  Pull_Resistor pull_resistor_4 (.node(pull_resistor_4_node));
  assign pull_resistor_4_node = and_2_out ? 4'b0010 : 4'bz;  // Controlled_Buffer controlled_buffer_4
  Multiplexer #(.select(3), .width(32)) multiplexer_1 (
    .in5(SP), .in6(LR_Value), .in7(PC), .out(multiplexer_1_out), .sel(Inst[5:3]));  // open: in0, in1, in2, in3, in4
  Multiplexer #(.select(3), .width(32)) multiplexer_2 (
    .in0(R0), .in1(R1), .in2(R2), .in3(R3), .in4(R4), .in5(R5), .in6(R6), .in7(R7), .out(multiplexer_2_out),
    .sel(Inst[5:3]));
  Shift_Add_Sub_Mov shift_add_sub_mov_1 (
    .Flags_Update_Mask(shift_add_sub_mov_1_flags_update_mask), .Carry(shift_add_sub_mov_1_carry),
    .Imm32_Enable(shift_add_sub_mov_1_imm32_enable), .Rm(shift_add_sub_mov_1_rm),
    .Rn(shift_add_sub_mov_1_rn), .Rd(shift_add_sub_mov_1_rd), .Imm5(Imm5), .Imm32(shift_add_sub_mov_1_imm32),
    .ALU_Opcode(shift_add_sub_mov_1_alu_opcode), .Instruction(Inst), .Enable(opcode_decoder_1_shift));
  Data_Processing data_processing_1 (
    .Rn(data_processing_1_rn), .Rm(data_processing_1_rm), .ALU_Opcode(data_processing_1_alu_opcode),
    .Flags_Update_Mask(data_processing_1_flags_update_mask), .Rd(data_processing_1_rd), .Instruction(Inst),
    .Enable(opcode_decoder_1_data_processing));
  Flags_APSR flags_apsr_1 (.Update_Mask(or_1_out), .Flags_In(FlagsIn), .Clk(Clk), .Rst(Reset), .Flags_Out(Flags));
  Load_Store load_store_1 (
    .Store(Store), .Load(Load), .PC_Hold(PC_Hold), .RAM_Addr(RAM_Addr), .Imm32(load_store_1_imm32),
    .Rmd(load_store_1_rmd), .Enable(opcode_decoder_1_load_store), .Old_Value(RAM_Value), .R7(R7), .R0(R0),
    .R1(R1), .R2(R2), .R3(R3), .R4(R4), .R5(R5), .R6(R6), .Program_Counter(PC), .Instruction(Inst),
    .Stack_Pointer(SP), .Clk(Clk), .Reset(Reset));
  Load_Address load_address_1 (
    .Enable(opcode_decoder_1_load_address), .Instruction(Inst), .Program_Counter(PC), .Stack_Pointer(SP),
    .Imm32_Enable(load_address_1_imm32_enable), .Rd(load_address_1_rd),
    .ALU_Opcode(load_address_1_alu_opcode), .Imm32(load_address_1_imm32));
  assign bit_extender_1_out = {{21{or_3_out[10]}}, or_3_out};  // Bit_Extender bit_extender_1
  assign or_3_out = conditional_1_offset | pull_resistor_1_node;  // OR_Gate or_3, 11 bits wide
  or or_4 (or_4_out, conditional_1_verified, and_1_out, opcode_decoder_1_long_branch, and_4_out);
  Register #(.width(32)) Link_Register (
    .D(adder_1_out), .en(opcode_decoder_1_long_branch), .clk(Clk), .Q(LR_Value));  // open: clr
  Adder #(.width(32)) adder_1 (.a(32'h1), .b(PC), .out(adder_1_out));  // open: cin, cout
  assign controlled_buffer_5_out = and_3_out ? negator_1_out : 32'bz;  // Controlled_Buffer controlled_buffer_5
  Negator #(.width(32)) negator_1 (.in(multiplexer_1_out), .out(negator_1_out));
  SP_Address sp_address_1 (
    .New_Stack_Pointer(sp_address_1_new_stack_pointer), .Write_Enable(sp_address_1_write_enable),
    .Stack_Pointer(SP), .Instruction(Inst), .Enable(opcode_decoder_1_sp_address));
  Adder #(.width(32)) adder_2 (.a(32'h2), .b(bit_extender_1_out), .out(adder_2_out));  // open: cin, cout
  or or_5 (or_5_out, conditional_1_verified, opcode_decoder_1_long_branch);
  Pull_Resistor pull_resistor_5 (.node(pull_resistor_5_node));
  assign pull_resistor_5_node = and_3_out ? 4'b1001 : 4'bz;  // Controlled_Buffer controlled_buffer_6
  Pull_Resistor pull_resistor_6 (.node(controlled_buffer_5_out));
  Adder #(.width(32)) adder_3 (.a(multiplexer_2_out), .b(32'h4), .out(adder_3_out));  // open: cin, cout
  Multiplier #(.width(32)) multiplier_1 (.a(32'h2), .b(adder_2_out), .out(multiplier_1_out));  // open: cin, cout
  Adder #(.width(32)) adder_4 (.a(multiplier_1_out), .b(PC), .out(adder_4_out), .cin(1'b0));  // open: cout
  assign and_5_out = ~32'h1 & adder_3_out;  // AND_Gate and_5, 32 bits wide
  assign controlled_buffer_7_out = and_4_out ? and_5_out : 32'bz;  // Controlled_Buffer controlled_buffer_7
  and and_6 (and_6_out, opcode_decoder_1_shift, ~opcode_decoder_1_data_processing);  // AND_Gate
  not not_1 (not_1_out, PC_Hold);
  assign controlled_buffer_8_out = or_5_out ? adder_4_out : 32'bz;  // Controlled_Buffer controlled_buffer_8
  Pull_Resistor pull_resistor_7 (.node(pull_resistor_7_node));
  assign pull_resistor_7_node = and_1_out ? LR_Value : 32'bz;  // Controlled_Buffer controlled_buffer_9
  Pull_Resistor pull_resistor_8 (.node(controlled_buffer_7_out));
  Multiplexer multiplexer_3 (.in0(Flags[1]), .in1(shift_add_sub_mov_1_carry), .out(Carry), .sel(and_6_out));
  Pull_Resistor pull_resistor_9 (.node(controlled_buffer_8_out));
  not not_2 (not_2_out, or_4_out);
  or or_6 (DP_Shift, and_6_out, opcode_decoder_1_high_register_op);
  or or_7 (Imm32_Enable, shift_add_sub_mov_1_imm32_enable, and_3_out, load_address_1_imm32_enable);
  assign Imm32 = shift_add_sub_mov_1_imm32 | load_store_1_imm32 | load_address_1_imm32 | controlled_buffer_5_out;  // OR_Gate or_8, 32 bits wide
  assign ALU_Opcode = shift_add_sub_mov_1_alu_opcode | data_processing_1_alu_opcode | pull_resistor_5_node | load_address_1_alu_opcode | pull_resistor_4_node;  // OR_Gate or_9, 4 bits wide
  assign Rm = shift_add_sub_mov_1_rm | data_processing_1_rm | load_store_1_rmd;  // OR_Gate or_10, 3 bits wide
  assign Rn = shift_add_sub_mov_1_rn | data_processing_1_rn | load_store_1_rmd | controlled_buffer_3_out;  // OR_Gate or_11, 3 bits wide
  assign Rd = shift_add_sub_mov_1_rd | data_processing_1_rd | controlled_buffer_2_out | load_store_1_rmd | load_address_1_rd;  // OR_Gate or_12, 3 bits wide
  assign or_13_out = controlled_buffer_8_out | pull_resistor_7_node | controlled_buffer_7_out;  // OR_Gate or_13, 32 bits wide
  Adder #(.width(32)) adder_5 (.a(PC), .b(32'h2), .out(adder_5_out));  // open: cin, cout
  Counter #(.max('hffffffff), .trigger("falling"), .width(32)) counter_1 (
    .clr(Reset), .load(not_1_out), .count(1'b0), .clk(Clk), .D(multiplexer_4_out), .Q(PC));  // open: up, carry
  Multiplexer #(.width(32)) multiplexer_4 (
    .in0(or_13_out), .in1(adder_5_out), .out(multiplexer_4_out), .sel(not_2_out));

  // Other names for the same wires on the sheet: PC_Value[31:0] = PC; SP_Value[31:0] = SP

  // Notes on the sheet:
  //   Extract carry
  //   Extract Opcode
  //   IF Reg_Imm=1 THEN use shift value from register ELSE use shift value from Imm5
  //   Buffer flags for next instruction
  //   Add 3 to offset because ARM pre-increments PC
  //   and does an additional prefetch operation
endmodule
